// Logisim project DSD PROJECT FINAL.circ as structural Verilog: 1 circuit, main circuit main
module main (
  input  in_1,
  input  in_2,
  input  TAP,
  input  R,
  output PUMP,
  output Q3,
  output Q2,
  output Q1,
  output Q0
);

  wire _0_qn, _1_qn, _2_qn, _3_qn, and_1_out, and_2_out, and_3_out, and_4_out, and_5_out, and_6_out,
       and_7_out, and_8_out, and_10_out, and_11_out, Clock_out, j_k_ff_1_q, not_1_out, not_2_out, or_1_out,
       or_2_out, or_3_out, or_4_out, or_5_out, or_6_out, xor_1_out, xor_2_out, xor_3_out, xor_4_out,
       xor_5_out;

  and and_1 (and_1_out, not_1_out, Q3, _2_qn, Q1, _0_qn);
  not not_1 (not_1_out, TAP);
  and and_2 (and_2_out, Q3, _2_qn, Q1, _0_qn);
  Clock Clock (.out(Clock_out));
  not not_2 (not_2_out, not_1_out);
  and and_3 (and_3_out, not_2_out, _0_qn);
  and and_4 (and_4_out, and_3_out, _1_qn);
  and and_5 (and_5_out, and_4_out, _2_qn);
  and and_6 (and_6_out, not_1_out, Q0);
  and and_7 (and_7_out, and_6_out, Q1);
  and and_8 (and_8_out, and_7_out, Q2);
  or or_1 (or_1_out, not_1_out, not_2_out);
  or or_2 (or_2_out, and_6_out, and_3_out);
  or or_3 (or_3_out, and_7_out, and_4_out);
  or or_4 (or_4_out, and_8_out, and_5_out);
  xor xor_1 (xor_1_out, Q0, or_1_out);
  xor xor_2 (xor_2_out, Q1, or_2_out);
  xor xor_3 (xor_3_out, Q2, or_3_out);
  xor xor_4 (xor_4_out, Q3, or_4_out);
  D_Flip_Flop _0 (.clk(Clock_out), .D(xor_1_out), .Q(Q0), .Qn(_0_qn), .preset(in_1), .en(xor_5_out), .reset(or_5_out));
  D_Flip_Flop _1 (
    .clk(Clock_out), .D(xor_2_out), .Q(Q1), .Qn(_1_qn), .preset(and_1_out), .en(xor_5_out), .reset(and_10_out));
  D_Flip_Flop _2 (.clk(Clock_out), .D(xor_3_out), .Q(Q2), .Qn(_2_qn), .preset(in_2), .en(xor_5_out), .reset(or_5_out));
  D_Flip_Flop _3 (
    .clk(Clock_out), .D(xor_4_out), .Q(Q3), .Qn(_3_qn), .preset(and_1_out), .en(xor_5_out), .reset(and_10_out));
  J_K_Flip_Flop j_k_ff_1 (
    .J(and_11_out), .clk(Clock_out), .K(and_2_out), .Q(j_k_ff_1_q), .en(R));  // open: Qn, preset, reset
  or or_5 (or_5_out, and_10_out, and_1_out);
  and and_9 (PUMP, j_k_ff_1_q, R);
  and and_10 (and_10_out, _3_qn, _2_qn, _1_qn, _0_qn, not_2_out);
  xor xor_5 (xor_5_out, not_2_out, PUMP);
  or or_6 (or_6_out, _1_qn, _0_qn);
  and and_11 (and_11_out, _3_qn, _2_qn, or_6_out);
endmodule
